# Fritzing sketch Temperature (saved by Fritzing 0.9.3b)
breadboards: 1

parts:
  R4 = Rotary Potentiometer (Small) [maximum_resistance=100kΩ package=THT]
  元件1 = Arduino Uno (Rev3) - ICSP
  U1 = LCD-16X2 [package=lcd-16x2]
  R6 = Resistor [tolerance=±5% resistance=10k package="0402 [SMD]"]
  J2 = Piezo Speaker
  DHT1 = DHT22 Humidity and Temperature Sensor
  U2 = ESP8266 WiFi Module [part_number=ESP8266]
  S1 = Momentary Switch [package=ksa_sealed_tac_switch]
  R7 = Resistor [tolerance=±5% resistance=10k package="0402 [SMD]"]

nets:
  5V: R4.leg1, 元件1.5V, R6.Pin_1, DHT1.VDD, R7.Pin_0
  GND: R4.leg2, 元件1.GND, J2.pin1, DHT1.GND, U2.GND, S1.4
  N1: 元件1.ICSP_MOSI, 元件1.D11_PWM/MOSI
  N2: 元件1.D8, J2.pin2
  N3: 元件1.D2, U2.TXD
  N4: 元件1.D3_PWM, U2.RXD
  N5: 元件1.D5_PWM, R6.Pin_0, DHT1.DATA
  N6: 元件1.D6_PWM, U1.E
  N7: 元件1.D7, S1.2, R7.Pin_1
  3V3: 元件1.3V3, U2.VCC, U2.RST, U2.CH_PD

custom parts:
  ESP8266 WiFi Module: Generic WiFi Module based on the ESP8266 with onboard PCB antenna and UART communications
